# Fritzing sketch SematikCizim (saved by Fritzing 0.9.3b)
breadboards: 1

parts:
  Raspberry_Pi_1 = Raspberry Pi 3 [part_number=RPI-3-V1.2]
  J1 = Basic Servo
  VCC1 = 4 x AAA Battery Mount

nets:
  N1: Raspberry_Pi_1.GPIO18, J1.pulse
  GND: Raspberry_Pi_1.GND, J1.gnd, VCC1.-

notes:
  picamera modülünü picamera slotuna koyunuz
  usb portuna web kamerasını bağlayınız
